# Fritzing sketch Car3 (saved by Fritzing 0.9.3b)
breadboards: 1

parts:
  Part1 = Arduino Uno (Rev3)  # not connected
  M1 = DC Motor  # not connected
  M2 = DC Motor  # not connected
  M3 = DC Motor  # not connected
  M4 = DC Motor  # not connected
  U1 = LIPO-2000mAh [package=lipo-2000]
  U2 = LIPO-2000mAh [package=lipo-2000]
  U3 = LIPO-2000mAh [package=lipo-2000]
  J1 = Piezo Speaker  # not connected
  Part2 = Arduino Modkit Shield  # not connected
  hc-sr1 = hc-sr04  # not connected
  J2 = Basic Servo  # not connected
  Part3 = Bluetooth HC-05 Macho  # not connected
  Part4 = DeuLigne 1.1 - The Snootlab's LCD shield for Arduino  # not connected

nets:
  N1: U1.+, U3.-
  N2: U1.-, U2.+
