# Fritzing sketch car2 circuit (saved by Fritzing 0.9.3b)
breadboards: 1

parts:
  Part1 = Arduino Uno (Rev3)
  Part3 = Arduino Motor Shield
  VCC2 = 4 x AAA Battery Mount
  M1 = DC Motor
  M2 = DC Motor
  VCC3 = 4 x AAA Battery Mount  # not connected
  J1 = Piezo Speaker  # not connected
  Front_IR = Infrared Proximity Sensor  # not connected
  Back_IR = Infrared Proximity Sensor  # not connected
  Left_IR = Infrared Proximity Sensor  # not connected
  Right_IR = Infrared Proximity Sensor  # not connected

nets:
  N1: Part1.D4, Part3.OUT1, M1.pin_2
  N2: Part1.D5_PWM, Part3.OUT2, M1.pin_1
  N3: Part1.D6_PWM, Part3.OUT4, M2.pin_1
  N4: Part1.D7, Part3.OUT3, M2.pin_2
  GND: Part1.GND, Part3.GND, VCC2.-
  VIN: Part1.VIN, Part3.VIN, VCC2.+
